# Fritzing sketch IotsaMotorServerBoard (saved by Fritzing 0.9.3b)

parts:
  Part1 = iotsa esp-12 experiment board
  IC1 = ULN2003A [package="DIP16 [THT]"]  # not connected
  R1 = Resistor [tolerance=±5% resistance=10k package=THT]  # not connected
  J2 = male pin header, 2 pins [form="♂ (male)"]
  28BYJ-48_5v_stepper = 28BYJ-48 Stepper Motor
  J3 = molex pin header, 5 pins [form=molex]  # not connected
  end-of-reel_microswitch = Pushbutton [package=THT]

nets:
  N1: Part1.pin_10, Part1.pin_90, Part1.pin_91
  N2: Part1.pin_13, Part1.pin_119, Part1.pin_120, Part1.pin_121, Part1.pin_134, Part1.pin_136
  N3: Part1.pin_14, Part1.pin_81, Part1.pin_82
  N4: Part1.pin_15, Part1.pin_84, Part1.pin_85
  N5: Part1.pin_16, Part1.pin_87, Part1.pin_88
  N6: Part1.pin_26, Part1.pin_74, Part1.pin_76
  N7: Part1.pin_27, Part1.pin_35, Part1.pin_47, Part1.pin_48, Part1.pin_71, Part1.pin_72, 28BYJ-48_5v_stepper.RED
  N8: Part1.pin_40, Part1.pin_45, Part1.pin_102, Part1.pin_103, Part1.pin_117, Part1.pin_118
  N9: Part1.pin_50, Part1.pin_51, 28BYJ-48_5v_stepper.ORANGE
  N10: Part1.pin_53, Part1.pin_54, 28BYJ-48_5v_stepper.YELLOW
  N11: Part1.pin_56, Part1.pin_57, 28BYJ-48_5v_stepper.PINK
  N12: Part1.pin_59, Part1.pin_60, 28BYJ-48_5v_stepper.BLUE
  N13: J2.pin1, end-of-reel_microswitch.leg1
  N14: J2.pin2, end-of-reel_microswitch.leg0

custom parts:
  iotsa esp-12 experiment board: Board with an ESP-12, a power supply, reset button, FTDI plug and experiment area.
  28BYJ-48 Stepper Motor: 28BYJ-48 gear-reduction stepper motor (small)
